# Fritzing sketch dron motores_ prueba 1_ conexion_drivers_conexion_MPU6050 (saved by Fritzing 0.9.3b)
breadboards: 1

parts:
  Componente1 = Adafruit TB6612 DC and Stepper Motor Driver [part_number="Adafruit #2448"]
  Componente2 = Adafruit TB6612 DC and Stepper Motor Driver [part_number="Adafruit #2448"]
  M1 = DC Motor
  M2 = DC Motor
  M3 = DC Motor
  M4 = DC Motor
  U1 = LIPO-1000mAh [package=lipo-1000]
  M5 = DOIT Esp32 DevKit v1 (30 pins long, 11 pins width) [part_number=ESP32S-PIN30]
  ESP32-CAM-CH1 = ESP32-CAM-CH340  # not connected
  Raspberry_Pi_B_rev1 = Raspberry Pi B rev1  # not connected
  GY1 = MPU-6050 Board GY-521 [form="♀ (female)" package=THT]

nets:
  N1: Componente1.PWRIN, Componente2.Vmotor, Componente2.PWRIN, U1.+
  GND: Componente1.GND, Componente2.GND, U1.-, M5.GND, GY1.pin2
  N2: Componente1.PWMB, M5.D15
  N3: Componente1.BIN2, M5.D19
  N4: Componente1.BIN1, M5.D18
  VCC: Componente1.STBY, Componente2.VCC, Componente2.STBY, M5.3V3, GY1.pin1
  N5: Componente1.AIN1, M5.D4
  N6: Componente1.AIN2, M5.RX2
  N7: Componente1.PWMA, M5.TX2
  N8: Componente1.MOTORA1, M4.pin_2
  N9: Componente1.MOTORA2, M4.pin_1
  N10: Componente1.MOTORB2, M3.pin_2
  N11: Componente1.MOTORB1, M3.pin_1
  N12: Componente2.PWMB, M5.D32
  N13: Componente2.BIN2, M5.D33
  N14: Componente2.BIN1, M5.D25
  N15: Componente2.AIN1, M5.D14
  N16: Componente2.AIN2, M5.D27
  N17: Componente2.PWMA, M5.D26
  N18: Componente2.MOTORA1, M1.pin_1
  N19: Componente2.MOTORA2, M1.pin_2
  N20: Componente2.MOTORB2, M2.pin_1
  N21: Componente2.MOTORB1, M2.pin_2
  N22: M5.D21, GY1.pin4
  N23: M5.D22, GY1.pin3

notes:
  MOTOR 1
  MOTOR 2
  Driver 1
  Driver 2
  MOTOR 3
  MOTOR 4
  MPU6050 Acelerometro+Giroscopio

custom parts:
  Adafruit TB6612 DC and Stepper Motor Driver: Spin two DC motors, step one bi-polar or uni-polar stepper, or fire off two solenoids with 1.2A per channel using the TB6612. These are perhaps better known as "the drivers in our assembled Adafruit Motorshield or Motor HAT." We really like these dual H-bridges, so if you want to control motors without a shield or HAT these are easy to include on any solderless breadboard or perma-proto.
  DOIT Esp32 DevKit v1 (30 pins long, 11 pins width): The DOIT Esp32 DevKit v1 is one of the development board created by DOIT to evaluate the ESP-WROOM-32 module. It is based on the ESP32 microcontroller that boasts Wifi, Bluetooth, Ethernet and Low Power support all in a single chip. (vanepp) made breadboard work, adjusted pin numbering and labels and reduced size of schematic and cleaned up pcb. This chip is 30pins long (2 x15) and 11 pins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
  ESP32-CAM-CH340: Versión de ESP-32-CAM que incluye puerto USB.
  MPU-6050 Board GY-521: Acelerometro y Giroscopio MPU-6050 Board GY-521

// code stored in the sketch: dron_ version1_motoresDC.ino
// MOTOR 1
#define AIN1 14
#define AIN2 27
#define PWMA 26

// MOTOR 2
#define BIN1 25
#define BIN2 33
#define PWMB 32

// MOTOR 3
#define AIN1_2 4
#define AIN2_2 16
#define PWMA_2 17

// MOTOR 4
#define BIN1_2 18
#define BIN2_2 19
#define PWMB_2 21

// Standby pin (activo en HIGH)
#define STBY 22

void setup() {
  // Pines de dirección y PWM
  pinMode(AIN1, OUTPUT);  pinMode(AIN2, OUTPUT);  pinMode(PWMA, OUTPUT);
  pinMode(BIN1, OUTPUT);  pinMode(BIN2, OUTPUT);  pinMode(PWMB, OUTPUT);
  pinMode(AIN1_2, OUTPUT); pinMode(AIN2_2, OUTPUT); pinMode(PWMA_2, OUTPUT);
  pinMode(BIN1_2, OUTPUT); pinMode(BIN2_2, OUTPUT); pinMode(PWMB_2, OUTPUT);
  pinMode(STBY, OUTPUT);

  digitalWrite(STBY, HIGH);  // Activa los drivers

  // Motores en marcha hacia adelante
  // M1
  digitalWrite(AIN1, HIGH);
  digitalWrite(AIN2, LOW);
  analogWrite(PWMA, 180);  // Velocidad 0-255

  // M2
  digitalWrite(BIN1, HIGH);
  digitalWrite(BIN2, LOW);
  analogWrite(PWMB, 180);

  // M3
  digitalWrite(AIN1_2, HIGH);
  digitalWrite(AIN2_2, LOW);
  analogWrite(PWMA_2, 180);

  // M4
  digitalWrite(BIN1_2, HIGH);
  digitalWrite(BIN2_2, LOW);
  analogWrite(PWMB_2, 180);
}

void loop() {
  // Todo queda girando en loop continuo
}
